# Fritzing sketch UnoBuild (saved by Fritzing 0.9.0b)
circuit board: 8.46667cm x 5.64444cm
breadboards: 1

parts:
  Part1 = Arduino Uno (Rev3)
  Q2 = NPN-Transistor [package="TO92 [THT]"]
  Q4 = NPN-Transistor [package="TO92 [THT]"]
  VCC1 = Battery block 9V
  Part2 = SRF05 Ultrasonic Rangefinder
  Q5 = NPN-Transistor [package="TO92 [THT]"]
  LED1 = LED - 5mm [color="Red (633nm)" package="5 mm [THT]"]
  LED2 = LED - 5mm [color="Red (633nm)" package="5 mm [THT]"]
  LED3 = LED - 5mm [color="Red (633nm)" package="5 mm [THT]"]

nets:
  N1: Part1.D8, Q5.B
  N2: Part1.D12/MISO, Part2.Echo
  N3: Part1.D13/SCK, Q2.B
  N4: Part1.D4, Part2.Trig
  N5: Part1.D7, Q4.B
  5V: Part1.5V, Part2.VCC
  GND: Part1.GND, Part2.GND
  N6: Q2.E, Q4.E, VCC1.-, Q5.E
  N7: Q2.C, LED3.anode
  N8: Q4.C, LED1.anode
  N9: VCC1.+, LED1.cathode, LED2.cathode, LED3.cathode
  N10: Q5.C, LED2.anode
